// Logisim project PB1204.circ as structural Verilog: 1 circuit, main circuit main
module main (
  input  in_1,
  input  [8:0] in_2,
  input  [3:0] DATAIN,
  output [3:0] DATAOUT,
  output [11:0] ADDRESS
);

  wire adder_1_cout, AddressRegister, AddressRegisterHigh, AddressRegisterLow, AddressRegisterMiddle, ALUADD,
       ALUNAND, ALUNOR, ALUNOT, ALUShiftLeft, ALUShiftRight, ALUSwap, and_1_out, and_2_out, and_3_out,
       and_4_out, and_5_out, and_6_out, and_7_out, and_8_out, and_9_out, and_10_out, and_11_out, and_12_out,
       and_13_out, and_14_out, and_15_out, and_16_out, and_17_out, and_18_out, and_19_out, and_20_out,
       and_21_out, and_22_out, and_23_out, and_24_out, and_25_out, and_26_out, and_27_out, ARegister,
       BRegister, clock_1_out, DecrementRegister, demultiplexer_2_out0, demultiplexer_2_out8,
       demultiplexer_3_out0, demultiplexer_3_out1, demultiplexer_3_out2, demultiplexer_3_out3,
       IncrementRegister, InstructionRegister, InterruptModeRegister, not_1_out, not_3_out, or_1_out,
       or_2_out, or_3_out, or_4_out, or_5_out, ProgramCounter, ProgramCounterHigh, ProgramCounterLow,
       ProgramCounterMiddle, pull_resistor_2_node, pull_resistor_3_node, pull_resistor_4_node,
       ReadFromALUOut, ReadFromDatabus, register_5_q, ResetRegister, StackPointer, StackPointerRegisterHigh,
       StackPointerRegisterLow, StackPointerRegisterMiddle, TriggerUpdate, WriteToDatabus;
  wire [2:0] register_1_q;
  wire [3:0] ABuffer_q, adder_1_out, ALUOut, AOut, BBuffer_q, BOut, controlled_buffer_1_out, DATABUS,
       InstructionCounter_q, InstructionRegister_q, nand_1_out, nor_1_out, not_2_out, ProgramCounterHigh_q,
       ProgramCounterLow_q, ProgramCounterMiddle_q, register_2_q, register_3_q, register_4_q;
  wire [11:0] controlled_buffer_7_out, ProgramCounterRegister_q, StackPointerRegister_q;

  Clock clock_1 (.out(clock_1_out));
  assign controlled_buffer_1_out = and_5_out ? ALUOut : 4'bz;  // Controlled_Buffer controlled_buffer_1
  and and_1 (and_1_out, ARegister, ReadFromDatabus);
  and and_2 (and_2_out, ARegister, TriggerUpdate);
  and and_3 (and_3_out, ARegister, WriteToDatabus);
  and and_4 (and_4_out, ARegister, ResetRegister);
  and and_5 (and_5_out, ARegister, ReadFromALUOut);
  and and_6 (and_6_out, BRegister, ReadFromDatabus);
  and and_7 (and_7_out, BRegister, TriggerUpdate);
  and and_8 (and_8_out, BRegister, WriteToDatabus);
  and and_9 (and_9_out, BRegister, ResetRegister);
  and and_10 (and_10_out, ResetRegister, InstructionRegister);
  Pull_Resistor pull_resistor_1 (.node(ReadFromDatabus));
  assign DATABUS = ReadFromDatabus ? DATAIN : 4'bz;  // Controlled_Buffer controlled_buffer_2
  not not_1 (not_1_out, ReadFromDatabus);
  assign DATAOUT = not_1_out ? DATABUS : 4'bz;  // Controlled_Buffer controlled_buffer_3
  Register #(.width(4)) ABuffer (
    .D(controlled_buffer_1_out), .en(or_1_out), .clk(or_1_out), .Q(ABuffer_q), .clr(and_4_out));
  assign controlled_buffer_1_out = and_1_out ? DATABUS : 4'bz;  // Controlled_Buffer controlled_buffer_4
  or or_1 (or_1_out, and_1_out, and_5_out);
  Register #(.width(4)) BBuffer (.D(DATABUS), .en(and_6_out), .clk(and_6_out), .Q(BBuffer_q), .clr(and_9_out));
  Counter #(.max('hf), .width(4)) InstructionCounter (
    .clr(and_10_out), .load(pull_resistor_2_node), .up(pull_resistor_3_node), .count(pull_resistor_4_node),
    .clk(clock_1_out), .Q(InstructionCounter_q));  // open: D, carry
  Pull_Resistor pull_resistor_2 (.node(pull_resistor_2_node));
  Pull_Resistor #(.pull(1)) pull_resistor_3 (.node(pull_resistor_3_node));
  Pull_Resistor #(.pull(1)) pull_resistor_4 (.node(pull_resistor_4_node));
  Register #(.width(4)) u_InstructionRegister (
    .D(DATABUS), .en(and_11_out), .clk(and_11_out), .Q(InstructionRegister_q), .clr(and_12_out));
  and and_11 (and_11_out, InstructionRegister, TriggerUpdate);
  and and_12 (and_12_out, InstructionRegister, ResetRegister);
  Pull_Resistor pull_resistor_5 (.node(DATABUS));
  Register #(.width(4)) u_ARegister (.D(ABuffer_q), .en(and_2_out), .clk(and_2_out), .Q(AOut), .clr(and_4_out));
  Register #(.width(4)) u_BRegister (.D(BBuffer_q), .en(and_7_out), .clk(and_7_out), .Q(BOut), .clr(and_9_out));
  ROM rom_1 (.addr({InstructionRegister_q, InstructionCounter_q}));  // open: data
  assign DATABUS = and_3_out ? AOut : 4'bz;  // Controlled_Buffer controlled_buffer_5
  assign DATABUS = and_8_out ? BOut : 4'bz;  // Controlled_Buffer controlled_buffer_6
  Register #(.width(4)) u_ProgramCounterLow (
    .D(DATABUS), .en(and_13_out), .clk(and_13_out), .Q(ProgramCounterLow_q));  // open: clr
  and and_13 (and_13_out, ProgramCounterLow, ReadFromDatabus);
  Register #(.width(4)) u_ProgramCounterMiddle (
    .D(DATABUS), .en(and_14_out), .clk(and_14_out), .Q(ProgramCounterMiddle_q));  // open: clr
  and and_14 (and_14_out, ProgramCounterMiddle, ReadFromDatabus);
  Register #(.width(4)) u_ProgramCounterHigh (
    .D(DATABUS), .en(and_15_out), .clk(and_15_out), .Q(ProgramCounterHigh_q));  // open: clr
  and and_15 (and_15_out, ProgramCounterHigh, ReadFromDatabus);
  and and_16 (and_16_out, ProgramCounter, TriggerUpdate);
  and and_17 (and_17_out, ProgramCounter, IncrementRegister);
  and and_18 (and_18_out, ProgramCounter, ResetRegister);
  Demultiplexer #(.select(4)) demultiplexer_1 (
    .out0(InstructionRegister), .out1(InterruptModeRegister), .out2(AddressRegisterLow),
    .out3(AddressRegisterMiddle), .out4(AddressRegisterHigh), .out5(ProgramCounter), .out6(StackPointer),
    .out7(AddressRegister), .out8(ARegister), .out9(BRegister), .out10(ProgramCounterLow),
    .out11(ProgramCounterMiddle), .out12(ProgramCounterHigh), .out13(StackPointerRegisterLow),
    .out14(StackPointerRegisterMiddle), .out15(StackPointerRegisterHigh), .in(in_1), .sel(in_2[3:0]));
  Demultiplexer #(.select(4)) demultiplexer_2 (
    .out0(demultiplexer_2_out0), .out1(ReadFromDatabus), .out2(WriteToDatabus), .out3(TriggerUpdate),
    .out4(IncrementRegister), .out5(DecrementRegister), .out6(ResetRegister), .out7(ReadFromALUOut),
    .out8(demultiplexer_2_out8), .out9(ALUNAND), .out10(ALUNOR), .out11(ALUNOT), .out12(ALUADD),
    .out13(ALUShiftLeft), .out14(ALUShiftRight), .out15(ALUSwap), .in(in_1), .sel(in_2[7:4]));
  Counter #(.max('hfff), .width(12)) ProgramCounterRegister (
    .clr(and_18_out), .load(and_16_out), .up(and_17_out), .clk(or_2_out),
    .D({ProgramCounterHigh_q, ProgramCounterMiddle_q, ProgramCounterLow_q}), .Q(ProgramCounterRegister_q));  // open: count, carry
  or or_2 (or_2_out, and_16_out, and_17_out);
  assign controlled_buffer_7_out = and_19_out ? ProgramCounterRegister_q : 12'bz;  // Controlled_Buffer controlled_buffer_7
  and and_19 (and_19_out, or_3_out, ProgramCounter);
  or or_3 (or_3_out, in_2[8], IncrementRegister);
  or or_4 (or_4_out, and_19_out, and_27_out);
  Register #(.width(3)) register_1 (.D(in_2[6:4]), .en(in_2[7]), .clk(in_2[7]), .Q(register_1_q));  // open: clr
  Register #(.width(4)) register_2 (.D(DATABUS), .en(and_20_out), .clk(and_20_out), .Q(register_2_q));  // open: clr
  and and_20 (and_20_out, StackPointerRegisterLow, ReadFromDatabus);
  Register #(.width(4)) register_3 (.D(DATABUS), .en(and_21_out), .clk(and_21_out), .Q(register_3_q));  // open: clr
  and and_21 (and_21_out, StackPointerRegisterMiddle, ReadFromDatabus);
  Register #(.width(4)) register_4 (.D(DATABUS), .en(and_22_out), .clk(and_22_out), .Q(register_4_q));  // open: clr
  and and_22 (and_22_out, StackPointerRegisterHigh, ReadFromDatabus);
  and and_23 (and_23_out, StackPointer, TriggerUpdate);
  and and_24 (and_24_out, StackPointer, ResetRegister);
  and and_25 (and_25_out, StackPointer, IncrementRegister);
  and and_26 (and_26_out, StackPointer, DecrementRegister);
  Demultiplexer #(.select(3)) demultiplexer_3 (
    .out0(demultiplexer_3_out0), .out1(demultiplexer_3_out1), .out2(demultiplexer_3_out2),
    .out3(demultiplexer_3_out3), .in(ReadFromALUOut), .sel(register_1_q));  // open: out4, out5, out6, out7
  assign nand_1_out = ~(AOut & BOut);  // NAND_Gate nand_1, 4 bits wide
  assign nor_1_out = ~(AOut | BOut);  // NOR_Gate nor_1, 4 bits wide
  assign not_2_out = ~AOut;  // NOT_Gate not_2, 4 bits wide
  Adder #(.width(4)) adder_1 (.a(AOut), .b(BOut), .out(adder_1_out), .cin(register_5_q), .cout(adder_1_cout));
  Register #(.trigger("falling"), .width(1)) register_5 (
    .D(adder_1_cout), .en(not_3_out), .clk(not_3_out), .Q(register_5_q));  // open: clr
  not not_3 (not_3_out, ALUADD);
  Counter #(.max('hfff), .width(12)) StackPointerRegister (
    .clr(and_24_out), .load(and_23_out), .up(and_25_out), .count(1'b1), .clk(or_5_out),
    .D({register_4_q, register_3_q, register_2_q}), .Q(StackPointerRegister_q));  // open: carry
  or or_5 (or_5_out, and_23_out, and_25_out, and_26_out);
  assign ALUOut = demultiplexer_3_out0 ? nand_1_out : 4'bz;  // Controlled_Buffer controlled_buffer_8
  assign ALUOut = demultiplexer_3_out1 ? nor_1_out : 4'bz;  // Controlled_Buffer controlled_buffer_9
  assign ALUOut = demultiplexer_3_out2 ? not_2_out : 4'bz;  // Controlled_Buffer controlled_buffer_10
  assign ALUOut = demultiplexer_3_out3 ? adder_1_out : 4'bz;  // Controlled_Buffer controlled_buffer_11
  Pull_Resistor pull_resistor_6 (.node(ALUOut));
  assign controlled_buffer_7_out = and_27_out ? StackPointerRegister_q : 12'bz;  // Controlled_Buffer controlled_buffer_12
  Counter #(.max('hfff), .width(12)) u_AddressRegister (
    .load(or_4_out), .clk(or_4_out), .D(controlled_buffer_7_out), .Q(ADDRESS));  // open: clr, up, count, carry
  and and_27 (and_27_out, in_2[8], StackPointer);

  // Other names for the same wires on the sheet: ALUmode[2:0] = in_2[6:4]; ALUenable = in_2[7];
  //   ADDRESSBUS[11:0] = ADDRESS; ConnectToAddressBus = in_2[8]; RW = ReadFromDatabus

  // Notes on the sheet:
  //   Nothing
  //   Nothing
endmodule
