// Logisim project PB1204alu.circ as structural Verilog: 1 circuit, main circuit pbp1204alu
module pbp1204alu (
  input  NANDenable,
  input  NORenable,
  input  NOTenable,
  input  ADDenable,
  input  SLenable,
  input  SRenable,
  input  PRIMARYenable,
  input  SECONDARYenable,
  input  [3:0] PrimaryInput,
  input  [3:0] SecondaryInput,
  input  CarryIn,
  output [3:0] PrimaryOutput,
  output CarryOut,
  output BorrowOut
);

  wire adder_1_cout, demultiplexer_1_out0, demultiplexer_1_out1, demultiplexer_1_out2, demultiplexer_1_out3,
       demultiplexer_1_out4, demultiplexer_1_out5, demultiplexer_1_out6, demultiplexer_1_out7,
       priority_encoder_1_gs;
  wire [0:0] pull_resistor_1_node;
  wire [2:0] ALUbuffer_q, priority_encoder_1_out;
  wire [3:0] adder_1_out, nand_1_out, nor_1_out, not_1_out;
  wire [3:3] pull_resistor_2_node;

  Priority_Encoder priority_encoder_1 (
    .in0(NANDenable), .in1(NORenable), .in2(NOTenable), .in3(ADDenable), .in4(SLenable), .in5(SRenable),
    .in6(PRIMARYenable), .in7(SECONDARYenable), .out(priority_encoder_1_out), .en_in(1'b1),
    .gs(priority_encoder_1_gs));  // open: en_out
  Register #(.width(3)) ALUbuffer (
    .D(priority_encoder_1_out), .en(priority_encoder_1_gs), .clk(priority_encoder_1_gs), .Q(ALUbuffer_q));  // open: clr
  Demultiplexer #(.select(3)) demultiplexer_1 (
    .out0(demultiplexer_1_out0), .out1(demultiplexer_1_out1), .out2(demultiplexer_1_out2),
    .out3(demultiplexer_1_out3), .out4(demultiplexer_1_out4), .out5(demultiplexer_1_out5),
    .out6(demultiplexer_1_out6), .out7(demultiplexer_1_out7), .in(1'b1), .sel(ALUbuffer_q));
  assign nand_1_out = ~(PrimaryInput & SecondaryInput);  // NAND_Gate nand_1, 4 bits wide
  assign nor_1_out = ~(PrimaryInput | SecondaryInput);  // NOR_Gate nor_1, 4 bits wide
  assign not_1_out = ~PrimaryInput;  // NOT_Gate not_1, 4 bits wide
  Adder #(.width(4)) adder_1 (
    .a(PrimaryInput), .b(SecondaryInput), .out(adder_1_out), .cin(CarryIn), .cout(adder_1_cout));
  Pull_Resistor pull_resistor_1 (.node(pull_resistor_1_node[0]));
  Pull_Resistor pull_resistor_2 (.node(pull_resistor_2_node[3]));
  assign PrimaryOutput = demultiplexer_1_out0 ? nand_1_out : 4'bz;  // Controlled_Buffer controlled_buffer_1
  assign PrimaryOutput = demultiplexer_1_out1 ? nor_1_out : 4'bz;  // Controlled_Buffer controlled_buffer_2
  assign PrimaryOutput = demultiplexer_1_out2 ? not_1_out : 4'bz;  // Controlled_Buffer controlled_buffer_3
  assign PrimaryOutput = demultiplexer_1_out3 ? adder_1_out : 4'bz;  // Controlled_Buffer controlled_buffer_4
  assign CarryOut = demultiplexer_1_out3 ? adder_1_cout : 1'bz;  // Controlled_Buffer controlled_buffer_5
  assign CarryOut = demultiplexer_1_out4 ? PrimaryInput[3] : 1'bz;  // Controlled_Buffer controlled_buffer_6
  assign PrimaryOutput = demultiplexer_1_out4 ? {PrimaryInput[2:0], pull_resistor_1_node[0]} : 4'bz;  // Controlled_Buffer controlled_buffer_7
  assign BorrowOut = demultiplexer_1_out5 ? PrimaryInput[0] : 1'bz;  // Controlled_Buffer controlled_buffer_8
  assign PrimaryOutput = demultiplexer_1_out5 ? {pull_resistor_2_node[3], PrimaryInput[3:1]} : 4'bz;  // Controlled_Buffer controlled_buffer_9
  assign PrimaryOutput = demultiplexer_1_out6 ? PrimaryInput : 4'bz;  // Controlled_Buffer controlled_buffer_10
  assign PrimaryOutput = demultiplexer_1_out7 ? SecondaryInput : 4'bz;  // Controlled_Buffer controlled_buffer_11
  Pull_Resistor pull_resistor_3 (.node(PrimaryOutput));
  Pull_Resistor pull_resistor_4 (.node(CarryOut));
  Pull_Resistor pull_resistor_5 (.node(BorrowOut));
endmodule
