// Logisim project PB1204microcode.circ as structural Verilog: 1 circuit, main circuit main
module main (
  input  [3:0] RegisterNumber,
  input  [3:0] FunctionNumber,
  input  [3:0] DATA,
  input  BitmaskEnable,
  input  ManualMode
);

  wire and_2_out, and_3_out, and_4_out, and_5_out, and_6_out, and_7_out, and_8_out, and_9_out, and_10_out,
       and_11_out, and_12_out, and_13_out, and_14_out, and_15_out, and_16_out, and_17_out, and_18_out,
       and_19_out, and_22_out, and_23_out, and_24_out, and_25_out, ARegisterEnable, Bitdepth,
       BitmaskEnable_t, BitmaskRegisterEnable, BorrowFlag, BorrowResult, BRegisterEnable,
       Buffer0RegisterEnable, Buffer1RegisterEnable, Buffer2RegisterEnable, CarryFlag, CarryResult,
       CheckIfFlag, CLK, comparator_1_eq, CycleReset, DecrementRegister, demultiplexer_2_out8,
       demultiplexer_2_out9, demultiplexer_2_out10, demultiplexer_2_out11, demultiplexer_2_out12,
       demultiplexer_2_out13, demultiplexer_2_out14, demultiplexer_2_out15, demultiplexer_3_out5,
       demultiplexer_3_out9, demultiplexer_3_out13, FlagsRegisterEnable, GeneralReset, HardwareReset,
       IncrementRegister, InstructionRegisterEnable, InterruptModeRegisterEnable, nor_1_out, not_2_out,
       not_3_out, not_4_out, not_5_out, not_6_out, or_1_out, or_2_out, or_3_out, or_4_out, or_6_out,
       or_7_out, or_8_out, or_11_out, or_12_out, or_13_out, or_14_out, PC0Enable, PC1Enable, PC2Enable,
       ReadFromBuffer, ReadFromDatabus, ResetRegister, s_r_ff_2_qn, s_r_ff_3_q, s_r_ff_3_qn, SkipMicrocode,
       SP0Enable, SP1Enable, SP2Enable, TestBorrowFlag, TestCarryFlag, TestFlagsRegisterEnable,
       TriggerUpdateOfRegister, WriteToAddressRegister, WriteToDatabus, xor_1_out, xor_2_out, xor_3_out;
  wire [3:0] AData, ALUData, and_1_out, BData, BitmaskRegister, Buffer0Register_q, Buffer1Data, Buffer2Data,
       controlled_buffer_17_out, CycleCounter, DATABUS, FlagsRegister, FuncID, InstructionRegister,
       InternalDatabus, InterruptModeRegister, MicrocodeRegister, PC0Data, PC1Data, PC2Data,
       pull_resistor_3_node, RegID, SP0Data, SP1Data, SP2Data, TestFlagsRegister;
  wire [8:0] Microcode_data;
  wire [11:0] ADDRESSBUS, controlled_buffer_19_out;

  nor nor_1 (nor_1_out, TestFlagsRegister[3], TestCarryFlag, TestBorrowFlag, TestFlagsRegister[0]);
  xor xor_1 (xor_1_out, AData[0], AData[1]);
  xor xor_2 (xor_2_out, AData[2], AData[3]);
  assign and_1_out = {TestFlagsRegister[3], TestCarryFlag, TestBorrowFlag, TestFlagsRegister[0]} & {FlagsRegister[3], CarryFlag, BorrowFlag, FlagsRegister[0]};  // AND_Gate and_1, 4 bits wide
  // Probe on AData
  // Probe on BData
  // Probe on CycleCounter
  // Probe on InstructionRegister
  // Probe on Bitdepth
  ROM #(.addrWidth(9), .dataWidth(9)) Microcode (
    .addr({Bitdepth, InstructionRegister, CycleCounter}), .data(Microcode_data));
  Register #(.trigger("high"), .width(4)) u_TestFlagsRegister (
    .D(InternalDatabus), .en(TestFlagsRegisterEnable), .clk(TriggerUpdateOfRegister),
    .Q({TestFlagsRegister[3], TestCarryFlag, TestBorrowFlag, TestFlagsRegister[0]}), .clr(HardwareReset));
  nor nor_2 (FlagsRegister[3], AData[0], AData[1], AData[2], AData[3]);
  xor xor_3 (xor_3_out, xor_1_out, xor_2_out);
  not not_1 (FlagsRegister[0], xor_3_out);
  or or_1 (or_1_out, nor_1_out, and_1_out[0], and_1_out[1], and_1_out[2], and_1_out[3]);
  RAM #(.addrWidth(12), .dataWidth(4), .databus("bidir"), .trigger("high"), .\type ("nonvolatile")) ram_1 (
    .addr(ADDRESSBUS), .we(WriteToDatabus), .oe(ReadFromDatabus), .data(DATABUS));
  and and_2 (and_2_out, CheckIfFlag, or_1_out);
  S_R_Flip_Flop s_r_ff_1 (.Q(SkipMicrocode), .reset(ResetRegister), .preset(and_2_out));  // open: S, R, clk, Qn
  assign {BitmaskEnable_t, FuncID, MicrocodeRegister} = ManualMode ? {BitmaskEnable, FunctionNumber, RegisterNumber} : 9'bz;  // Controlled_Buffer controlled_buffer_1
  not not_2 (not_2_out, ManualMode);
  Pull_Resistor pull_resistor_1 (.node({BitmaskEnable_t, FuncID, MicrocodeRegister}));
  assign {BitmaskEnable_t, FuncID, MicrocodeRegister} = not_2_out ? Microcode_data : 9'bz;  // Controlled_Buffer controlled_buffer_2
  // Probe on DATABUS
  Clock clock_1 (.out(CLK));
  Pull_Resistor pull_resistor_2 (.node(DATABUS));
  and and_3 (and_3_out, CLK, FuncID[3]);
  // Probe on MicrocodeRegister
  // Probe on FuncID
  // Probe on BitmaskEnable_t
  or or_2 (or_2_out, ReadFromBuffer, and_3_out);
  and and_4 (and_4_out, TestFlagsRegisterEnable, ResetRegister, TestBorrowFlag);
  assign RegID = not_3_out ? MicrocodeRegister : 4'bz;  // Controlled_Buffer controlled_buffer_3
  not not_3 (not_3_out, BitmaskEnable_t);
  assign RegID = BitmaskEnable_t ? BitmaskRegister : 4'bz;  // Controlled_Buffer controlled_buffer_4
  Pull_Resistor pull_resistor_3 (.node(pull_resistor_3_node));
  assign pull_resistor_3_node = or_2_out ? ALUData : 4'bz;  // Controlled_Buffer controlled_buffer_5
  or or_3 (or_3_out, or_2_out, ReadFromDatabus);
  assign pull_resistor_3_node = ReadFromDatabus ? DATABUS : 4'bz;  // Controlled_Buffer controlled_buffer_6
  S_R_Flip_Flop #(.trigger("high")) BorrowRegister (
    .S(BorrowResult), .R(not_4_out), .clk(and_5_out), .Q(BorrowFlag), .reset(or_4_out));  // open: Qn, preset
  not not_4 (not_4_out, BorrowResult);
  and and_5 (and_5_out, CLK, FuncID[3]);
  or or_4 (or_4_out, and_4_out, HardwareReset);
  and and_6 (and_6_out, WriteToDatabus, ARegisterEnable);
  and and_7 (and_7_out, WriteToDatabus, PC0Enable);
  assign DATABUS = and_6_out ? AData : 4'bz;  // Controlled_Buffer controlled_buffer_7
  and and_8 (and_8_out, WriteToDatabus, PC1Enable);
  and and_9 (and_9_out, WriteToDatabus, PC2Enable);
  assign DATABUS = and_7_out ? PC0Data : 4'bz;  // Controlled_Buffer controlled_buffer_8
  assign DATABUS = and_8_out ? PC1Data : 4'bz;  // Controlled_Buffer controlled_buffer_9
  assign DATABUS = and_9_out ? PC2Data : 4'bz;  // Controlled_Buffer controlled_buffer_10
  Register #(.trigger("high"), .width(4)) Buffer0Register (
    .D(pull_resistor_3_node), .en(Buffer0RegisterEnable), .clk(or_3_out), .Q(Buffer0Register_q),
    .clr(HardwareReset));
  Register #(.trigger("high"), .width(4)) Buffer1Register (
    .D(pull_resistor_3_node), .en(Buffer1RegisterEnable), .clk(or_3_out), .Q(Buffer1Data), .clr(HardwareReset));
  Register #(.trigger("high"), .width(4)) Buffer2Register (
    .D(pull_resistor_3_node), .en(Buffer2RegisterEnable), .clk(or_3_out), .Q(Buffer2Data), .clr(HardwareReset));
  and and_10 (and_10_out, WriteToDatabus, BRegisterEnable);
  and and_11 (and_11_out, WriteToDatabus, SP0Enable);
  and and_12 (and_12_out, WriteToDatabus, SP1Enable);
  assign DATABUS = and_10_out ? BData : 4'bz;  // Controlled_Buffer controlled_buffer_11
  assign DATABUS = and_11_out ? SP0Data : 4'bz;  // Controlled_Buffer controlled_buffer_12
  assign DATABUS = and_12_out ? SP1Data : 4'bz;  // Controlled_Buffer controlled_buffer_13
  or or_5 (TriggerUpdateOfRegister, ReadFromBuffer, ReadFromDatabus);
  and and_13 (and_13_out, WriteToDatabus, SP2Enable);
  assign DATABUS = and_13_out ? SP2Data : 4'bz;  // Controlled_Buffer controlled_buffer_14
  Register #(.trigger("high"), .width(4)) u_InstructionRegister (
    .D(InternalDatabus), .en(InstructionRegisterEnable), .clk(and_14_out), .Q(InstructionRegister),
    .clr(GeneralReset));
  and and_14 (and_14_out, InstructionRegisterEnable, TriggerUpdateOfRegister);
  assign InternalDatabus = ReadFromDatabus ? DATABUS : 4'bz;  // Controlled_Buffer controlled_buffer_15
  assign InternalDatabus = or_6_out ? Buffer0Register_q : 4'bz;  // Controlled_Buffer controlled_buffer_16
  Pull_Resistor pull_resistor_4 (.node(InternalDatabus));
  or or_6 (or_6_out, ReadFromBuffer, WriteToAddressRegister);
  not not_5 (not_5_out, CarryResult);
  Counter #(.max('hf), .trigger("falling"), .width(4)) u_CycleCounter (
    .clr(CycleReset), .clk(CLK), .Q(CycleCounter));  // open: load, up, count, D, carry
  Pull_Resistor pull_resistor_5 (.node(InstructionRegister));
  S_R_Flip_Flop #(.trigger("high")) CarryRegister (
    .S(CarryResult), .R(not_5_out), .clk(and_5_out), .Q(CarryFlag), .reset(or_7_out));  // open: Qn, preset
  and and_15 (and_15_out, TestFlagsRegisterEnable, ResetRegister, TestCarryFlag);
  or or_7 (or_7_out, and_15_out, HardwareReset);
  Demultiplexer #(.select(4)) demultiplexer_1 (
    .out0(InstructionRegisterEnable), .out1(BitmaskRegisterEnable), .out2(FlagsRegisterEnable),
    .out3(TestFlagsRegisterEnable), .out4(InterruptModeRegisterEnable), .out5(Buffer0RegisterEnable),
    .out6(Buffer1RegisterEnable), .out7(Buffer2RegisterEnable), .out8(ARegisterEnable), .out9(PC0Enable),
    .out10(PC1Enable), .out11(PC2Enable), .out12(BRegisterEnable), .out13(SP0Enable), .out14(SP1Enable),
    .out15(SP2Enable), .in(CLK), .sel(RegID));
  Demultiplexer #(.select(4)) demultiplexer_2 (
    .out0(ReadFromDatabus), .out1(WriteToDatabus), .out2(WriteToAddressRegister), .out3(ReadFromBuffer),
    .out4(IncrementRegister), .out5(DecrementRegister), .out6(CheckIfFlag), .out7(ResetRegister),
    .out8(demultiplexer_2_out8), .out9(demultiplexer_2_out9), .out10(demultiplexer_2_out10),
    .out11(demultiplexer_2_out11), .out12(demultiplexer_2_out12), .out13(demultiplexer_2_out13),
    .out14(demultiplexer_2_out14), .out15(demultiplexer_2_out15), .in(CLK), .sel(FuncID));
  or or_8 (or_8_out, TriggerUpdateOfRegister, IncrementRegister);
  Counter #(.max('hf), .width(4)) u_BitmaskRegister (
    .clr(HardwareReset), .load(TriggerUpdateOfRegister), .up(1'b1), .count(1'b1), .clk(and_16_out),
    .D(InternalDatabus), .Q(BitmaskRegister));  // open: carry
  and and_16 (and_16_out, BitmaskRegisterEnable, or_8_out);
  Comparator #(.mode("unsigned"), .width(4)) comparator_1 (
    .a(InstructionRegister), .b(4'b1001), .eq(comparator_1_eq));  // open: gt, lt
  Register #(.trigger("high"), .width(4)) u_InterruptModeRegister (
    .D(InternalDatabus), .en(InterruptModeRegisterEnable), .clk(and_17_out), .Q(InterruptModeRegister),
    .clr(HardwareReset));
  and and_17 (and_17_out, InterruptModeRegisterEnable, TriggerUpdateOfRegister);
  and and_18 (and_18_out, ARegisterEnable, TriggerUpdateOfRegister);
  assign controlled_buffer_17_out = comparator_1_eq ? AData : 4'bz;  // Controlled_Buffer controlled_buffer_17
  not not_6 (not_6_out, comparator_1_eq);
  assign controlled_buffer_17_out = not_6_out ? InternalDatabus : 4'bz;  // Controlled_Buffer controlled_buffer_18
  and and_19 (and_19_out, BRegisterEnable, TriggerUpdateOfRegister);
  and and_20 (CycleReset, ResetRegister, FlagsRegisterEnable);
  and and_21 (HardwareReset, ResetRegister, InstructionRegisterEnable);
  Demultiplexer #(.select(4)) demultiplexer_3 (
    .out5(demultiplexer_3_out5), .out9(demultiplexer_3_out9), .out13(demultiplexer_3_out13), .in(1'b1),
    .sel(BitmaskRegister));  // open: out0, out1, out2, out3, out4, out6, out7, out8, out10, out11, out12, out14, out15
  Register #(.trigger("high"), .width(4)) ARegister (
    .D(InternalDatabus), .en(ARegisterEnable), .clk(and_18_out), .Q(AData), .clr(HardwareReset));
  Register #(.trigger("high"), .width(4)) BRegister (
    .D(controlled_buffer_17_out), .en(BRegisterEnable), .clk(and_19_out), .Q(BData), .clr(HardwareReset));
  Pull_Resistor pull_resistor_6 (.node(ALUData));
  pbp1204alu pbp1204alu_1 (
    .NANDenable(demultiplexer_2_out8), .NORenable(demultiplexer_2_out9), .NOTenable(demultiplexer_2_out10),
    .ADDenable(demultiplexer_2_out11), .SLenable(demultiplexer_2_out12), .SRenable(demultiplexer_2_out13),
    .PRIMARYenable(demultiplexer_2_out14), .SECONDARYenable(demultiplexer_2_out15), .PrimaryInput(AData),
    .SecondaryInput(BData), .CarryIn(CarryFlag), .PrimaryOutput(ALUData), .CarryOut(CarryResult),
    .BorrowOut(BorrowResult));
  or or_9 (GeneralReset, CycleReset, HardwareReset);
  or or_10 (Bitdepth, demultiplexer_3_out5, demultiplexer_3_out9, demultiplexer_3_out13);
  Pull_Resistor pull_resistor_7 (.node(Bitdepth));
  S_R_Flip_Flop s_r_ff_2 (
    .reset(IncrementRegister), .Qn(s_r_ff_2_qn), .preset(DecrementRegister));  // open: S, R, clk, Q
  or or_11 (or_11_out, IncrementRegister, IncrementRegister);
  and and_22 (and_22_out, PC0Enable, SkipMicrocode, TriggerUpdateOfRegister);
  and and_23 (and_23_out, PC0Enable, or_11_out);
  or or_12 (or_12_out, and_22_out, and_23_out, CycleReset);
  Counter #(.max('hfff), .width(12)) ProgramCounter (
    .clr(HardwareReset), .load(and_22_out), .up(s_r_ff_2_qn), .count(1'b1), .clk(or_12_out),
    .D({Buffer2Data, Buffer1Data, InternalDatabus}), .Q({PC2Data, PC1Data, PC0Data}));  // open: carry
  assign controlled_buffer_19_out = and_24_out ? {PC2Data, PC1Data, PC0Data} : 12'bz;  // Controlled_Buffer controlled_buffer_19
  and and_24 (and_24_out, s_r_ff_3_qn, or_12_out);
  assign controlled_buffer_19_out = s_r_ff_3_q ? {Buffer2Data, Buffer1Data, InternalDatabus} : 12'bz;  // Controlled_Buffer controlled_buffer_20
  and and_25 (and_25_out, Buffer0RegisterEnable, IncrementRegister);
  or or_13 (or_13_out, or_12_out, WriteToAddressRegister);
  or or_14 (or_14_out, and_25_out, or_13_out);
  S_R_Flip_Flop s_r_ff_3 (.Q(s_r_ff_3_q), .Qn(s_r_ff_3_qn), .preset(WriteToAddressRegister));  // open: S, R, clk, reset
  Counter #(.max('hfff), .trigger("falling"), .width(12)) AddressRegister (
    .clr(HardwareReset), .load(s_r_ff_3_q), .up(1'b1), .count(1'b1), .clk(or_14_out),
    .D(controlled_buffer_19_out), .Q(ADDRESSBUS));  // open: carry

  // Other names for the same wires on the sheet: OddParityFlag = FlagsRegister[0];
  //   FlagsRegister[2:1] = {CarryFlag, BorrowFlag}; ZeroFlag = FlagsRegister[3];
  //   TestOddParityFlag = TestFlagsRegister[0]; TestFlagsRegister[2:1] = {TestCarryFlag, TestBorrowFlag};
  //   TestZeroFlag = TestFlagsRegister[3]

  // Notes on the sheet:
  //   Passive Flags
  //   contents of Microcode (hex, n*v repeats v):
  //   0 85 38 72 13*0 95 38 72 13*0 a5 38 72 13*0 b5 38 72 13*0 c5 38 72 13*0 d5 38 72 13*0 49 1 49 100 72
  //   11*0 49 5 49 6 49 7 49 1 25 110 72 5*0 49 5 49 6 49 7 49 1 25 100 72 5*0 f5 3c 38 72 76*0 49 5 49 6
  //   49 7 49 3 63 39 72 5*0 49 3 73 72 48*0 20 82*0 1 25 110 29*0 1 20
  //   Conditionals
  //   Register Outputs to Databus
  //   Active Flags
  //   Decoder
  //   Arithmetic Registers
  //   Reset Handling
  //   ALU
  //   CAN DEFINITELY BE SIMPLIFIED
  //   BODGE: Address Register needs to be incremented seperately for some things!!
endmodule
