// Logisim project 12BitIncrementAndDecrementCounterWithLoadAndSetReset.circ as structural Verilog: 1 circuit, main circuit WideCounterWithSR
module WideCounterWithSR (
  input  LOAD,
  input  RESET,
  input  SET,
  input  UPDOWN,
  input  [11:0] DATA,
  input  CLK,
  input  NXTIN,
  output [11:0] DATAOUT,
  output NXTOUT
);

  wire nibbleincrementanddecrementcounterwithloadandsetreset_1_carryouthigh,
       nibbleincrementanddecrementcounterwithloadandsetreset_1_carryoutlow,
       nibbleincrementanddecrementcounterwithloadandsetreset_1_nxtout,
       nibbleincrementanddecrementcounterwithloadandsetreset_2_carryouthigh,
       nibbleincrementanddecrementcounterwithloadandsetreset_2_carryoutlow,
       nibbleincrementanddecrementcounterwithloadandsetreset_2_nxtout, not_1_out;

  not not_1 (not_1_out, UPDOWN);
  NibbleIncrementAndDecrementCounterWithLoadAndSetReset nibbleincrementanddecrementcounterwithloadandsetreset_1 (
    .D(DATA[3:0]), .LOAD(LOAD), .RESET(RESET), .SET(SET), .CarryInHigh(not_1_out), .NXTIN(NXTIN), .CLK(CLK),
    .CarryInLow(UPDOWN), .DATAOUT(DATAOUT[3:0]),
    .CarryOutHigh(nibbleincrementanddecrementcounterwithloadandsetreset_1_carryouthigh),
    .NXTOUT(nibbleincrementanddecrementcounterwithloadandsetreset_1_nxtout),
    .CarryOutLow(nibbleincrementanddecrementcounterwithloadandsetreset_1_carryoutlow));
  NibbleIncrementAndDecrementCounterWithLoadAndSetReset nibbleincrementanddecrementcounterwithloadandsetreset_2 (
    .D(DATA[7:4]), .LOAD(LOAD), .RESET(RESET), .SET(SET),
    .CarryInHigh(nibbleincrementanddecrementcounterwithloadandsetreset_1_carryouthigh),
    .NXTIN(nibbleincrementanddecrementcounterwithloadandsetreset_1_nxtout), .CLK(CLK),
    .CarryInLow(nibbleincrementanddecrementcounterwithloadandsetreset_1_carryoutlow), .DATAOUT(DATAOUT[7:4]),
    .CarryOutHigh(nibbleincrementanddecrementcounterwithloadandsetreset_2_carryouthigh),
    .NXTOUT(nibbleincrementanddecrementcounterwithloadandsetreset_2_nxtout),
    .CarryOutLow(nibbleincrementanddecrementcounterwithloadandsetreset_2_carryoutlow));
  NibbleIncrementAndDecrementCounterWithLoadAndSetReset nibbleincrementanddecrementcounterwithloadandsetreset_3 (
    .D(DATA[11:8]), .LOAD(LOAD), .RESET(RESET), .SET(SET),
    .CarryInHigh(nibbleincrementanddecrementcounterwithloadandsetreset_2_carryouthigh),
    .NXTIN(nibbleincrementanddecrementcounterwithloadandsetreset_2_nxtout), .CLK(CLK),
    .CarryInLow(nibbleincrementanddecrementcounterwithloadandsetreset_2_carryoutlow),
    .DATAOUT(DATAOUT[11:8]), .NXTOUT(NXTOUT));  // open: CarryOutHigh, CarryOutLow
endmodule
