// Logisim project 12BitRegisterWithSetReset.circ as structural Verilog: 1 circuit, main circuit WideRegisterWithSetReset
module WideRegisterWithSetReset (
  input  WE,
  input  CLK,
  input  S,
  input  [11:0] DATA,
  input  R,
  output [11:0] Q
);

  NibbleRegisterWithSetReset nibbleregisterwithsetreset_1 (
    .WE(WE), .CLK(CLK), .S(S), .DATA(DATA[3:0]), .R(R), .Q(Q[3:0]));
  NibbleRegisterWithSetReset nibbleregisterwithsetreset_2 (
    .WE(WE), .CLK(CLK), .S(S), .DATA(DATA[7:4]), .R(R), .Q(Q[7:4]));
  NibbleRegisterWithSetReset nibbleregisterwithsetreset_3 (
    .WE(WE), .CLK(CLK), .S(S), .DATA(DATA[11:8]), .R(R), .Q(Q[11:8]));
endmodule
