// Logisim project 4BitIncrementAndDecrementCounterWithLoadAndSetReset.circ as structural Verilog: 1 circuit, main circuit NibbleIncrementAndDecrementCounterWithLoadAndSetReset
module NibbleIncrementAndDecrementCounterWithLoadAndSetReset (
  input  [3:0] D,
  input  LOAD,
  input  RESET,
  input  SET,
  input  UPDOWN,
  input  NXTIN,
  input  CLK,
  output [3:0] DATAOUT,
  output NXTOUT
);

  wire and_1_out, and_2_out, and_3_out, and_4_out, and_5_out, and_6_out, and_7_out, and_8_out, and_9_out,
       j_k_ff_1_qn, j_k_ff_2_qn, j_k_ff_3_qn, j_k_ff_4_qn, nand_1_out, nand_2_out, nand_3_out, nand_4_out,
       nand_5_out, nand_6_out, nand_7_out, nand_8_out, nor_1_out, nor_2_out, nor_3_out, nor_4_out, nor_5_out,
       nor_6_out, nor_7_out, nor_8_out, not_1_out, not_2_out, not_3_out, not_4_out, not_5_out, not_6_out,
       or_1_out, or_2_out, or_3_out;

  not not_1 (not_1_out, UPDOWN);
  and and_1 (and_1_out, LOAD, CLK);
  nor nor_1 (nor_1_out, SET, nand_1_out);
  J_K_Flip_Flop j_k_ff_1 (
    .J(NXTIN), .K(NXTIN), .clk(CLK), .Q(DATAOUT[3]), .Qn(j_k_ff_1_qn), .preset(nor_1_out), .reset(nor_2_out));
  not not_2 (not_2_out, not_1_out);
  not not_3 (not_3_out, D[0]);
  nand nand_1 (nand_1_out, and_1_out, D[0]);
  nand nand_2 (nand_2_out, and_1_out, not_3_out);
  nor nor_2 (nor_2_out, RESET, nand_2_out);
  and and_2 (and_2_out, not_1_out, DATAOUT[3]);
  and and_3 (and_3_out, j_k_ff_1_qn, not_2_out);
  nor nor_3 (nor_3_out, SET, nand_3_out);
  J_K_Flip_Flop j_k_ff_2 (
    .J(or_1_out), .K(or_1_out), .clk(CLK), .Q(DATAOUT[2]), .Qn(j_k_ff_2_qn), .preset(nor_3_out),
    .reset(nor_4_out));
  or or_1 (or_1_out, and_2_out, and_3_out);
  not not_4 (not_4_out, D[1]);
  nand nand_3 (nand_3_out, and_1_out, D[1]);
  nand nand_4 (nand_4_out, and_1_out, not_4_out);
  nor nor_4 (nor_4_out, RESET, nand_4_out);
  and and_4 (and_4_out, and_2_out, DATAOUT[2]);
  and and_5 (and_5_out, j_k_ff_2_qn, and_3_out);
  nor nor_5 (nor_5_out, SET, nand_5_out);
  J_K_Flip_Flop j_k_ff_3 (
    .J(or_2_out), .K(or_2_out), .clk(CLK), .Q(DATAOUT[1]), .Qn(j_k_ff_3_qn), .preset(nor_5_out),
    .reset(nor_6_out));
  or or_2 (or_2_out, and_4_out, and_5_out);
  not not_5 (not_5_out, D[2]);
  nand nand_5 (nand_5_out, and_1_out, D[2]);
  nand nand_6 (nand_6_out, and_1_out, not_5_out);
  nor nor_6 (nor_6_out, RESET, nand_6_out);
  and and_6 (and_6_out, and_4_out, DATAOUT[1]);
  and and_7 (and_7_out, j_k_ff_3_qn, and_5_out);
  nor nor_7 (nor_7_out, SET, nand_8_out);
  J_K_Flip_Flop j_k_ff_4 (
    .J(or_3_out), .K(or_3_out), .clk(CLK), .Q(DATAOUT[0]), .Qn(j_k_ff_4_qn), .preset(nor_7_out),
    .reset(nor_8_out));
  or or_3 (or_3_out, and_6_out, and_7_out);
  not not_6 (not_6_out, D[3]);
  nand nand_7 (nand_7_out, and_1_out, not_6_out);
  nand nand_8 (nand_8_out, and_1_out, D[3]);
  nor nor_8 (nor_8_out, RESET, nand_7_out);
  and and_8 (and_8_out, and_6_out, DATAOUT[0]);
  and and_9 (and_9_out, j_k_ff_4_qn, and_7_out);
  or or_4 (NXTOUT, and_8_out, and_9_out);
endmodule
