// Logisim project 4BitRegisterWithSetReset.circ as structural Verilog: 1 circuit, main circuit NibbleRegisterWithSetReset
module NibbleRegisterWithSetReset (
  input  WE,
  input  CLK,
  input  S,
  input  [3:0] DATA,
  input  R,
  output [3:0] Q
);

  wire and_1_out;

  and and_1 (and_1_out, WE, CLK);
  EdgeTriggeredDflipflopWithSetAndReset edgetriggereddflipflopwithsetandreset_1 (
    .SET(S), .CLK(and_1_out), .DATA(DATA[0]), .RESET(R), .Q(Q[0]));  // open: Qinv
  EdgeTriggeredDflipflopWithSetAndReset edgetriggereddflipflopwithsetandreset_2 (
    .SET(S), .CLK(and_1_out), .DATA(DATA[1]), .RESET(R), .Q(Q[1]));  // open: Qinv
  EdgeTriggeredDflipflopWithSetAndReset edgetriggereddflipflopwithsetandreset_3 (
    .SET(S), .CLK(and_1_out), .DATA(DATA[2]), .RESET(R), .Q(Q[2]));  // open: Qinv
  EdgeTriggeredDflipflopWithSetAndReset edgetriggereddflipflopwithsetandreset_4 (
    .SET(S), .CLK(and_1_out), .DATA(DATA[3]), .RESET(R), .Q(Q[3]));  // open: Qinv
  Pull_Resistor pull_resistor_1 (.node(Q));
endmodule
