// Logisim project EdgeTriggeredDflipflopWithSetAndReset.circ as structural Verilog: 1 circuit, main circuit EdgeTriggeredDflipflopWithSetAndReset
module EdgeTriggeredDflipflopWithSetAndReset (
  input  SET,
  input  CLK,
  input  DATA,
  input  RESET,
  output Q,
  output Qinv
);

  wire nand_1_out, nand_2_out, nand_3_out, nand_4_out, not_1_out, not_2_out;

  not not_1 (not_1_out, SET);
  not not_2 (not_2_out, RESET);
  nand nand_1 (nand_1_out, not_1_out, nand_4_out, nand_2_out);
  nand nand_2 (nand_2_out, nand_1_out, CLK, not_2_out);
  nand nand_3 (nand_3_out, nand_2_out, CLK, nand_4_out);
  nand nand_4 (nand_4_out, nand_3_out, DATA, not_2_out);
  nand nand_5 (Q, not_1_out, nand_2_out, Qinv);
  nand nand_6 (Qinv, Q, nand_3_out, not_2_out);
endmodule
