// Logisim project 12bitIncrementDecrement.circ as structural Verilog: 1 circuit, main circuit main
module main (
  input  LOAD,
  input  UPDOWN,
  input  AB,
  input  SP,
  input  PC,
  input  EN,
  input  CLK
);

  wire and_1_out, and_2_out, and_3_out, not_1_out, not_2_out, pull_resistor_2_node;
  wire [11:0] adder_1_out, AddressBuffer_q, controlled_buffer_1_out, controlled_buffer_4_out,
       controlled_buffer_6_out, ProgramCounter_q, StackPointer_q;

  and and_1 (and_1_out, EN, PC);
  and and_2 (and_2_out, EN, SP);
  and and_3 (and_3_out, EN, AB);
  Register #(.trigger("falling"), .width(12)) ProgramCounter (
    .D(controlled_buffer_6_out), .en(and_1_out), .clk(CLK), .Q(ProgramCounter_q));  // open: clr
  Register #(.trigger("falling"), .width(12)) StackPointer (
    .D(controlled_buffer_6_out), .en(and_2_out), .clk(CLK), .Q(StackPointer_q));  // open: clr
  Register #(.trigger("falling"), .width(12)) AddressBuffer (
    .D(controlled_buffer_6_out), .en(and_3_out), .clk(CLK), .Q(AddressBuffer_q));  // open: clr
  assign controlled_buffer_1_out = PC ? ProgramCounter_q : 12'bz;  // Controlled_Buffer controlled_buffer_1
  assign controlled_buffer_1_out = SP ? StackPointer_q : 12'bz;  // Controlled_Buffer controlled_buffer_2
  Pull_Resistor pull_resistor_1 (.node(controlled_buffer_1_out));
  assign controlled_buffer_1_out = AB ? AddressBuffer_q : 12'bz;  // Controlled_Buffer controlled_buffer_3
  not not_1 (not_1_out, UPDOWN);
  Pull_Resistor pull_resistor_2 (.node(pull_resistor_2_node));
  Adder #(.width(12)) adder_1 (
    .a(controlled_buffer_1_out), .b(controlled_buffer_4_out), .out(adder_1_out), .cin(pull_resistor_2_node));  // open: cout
  assign controlled_buffer_4_out = UPDOWN ? 12'h1 : 12'bz;  // Controlled_Buffer controlled_buffer_4
  assign controlled_buffer_4_out = not_1_out ? {12{1'b1}} : 12'bz;  // Controlled_Buffer controlled_buffer_5
  not not_2 (not_2_out, LOAD);
  assign controlled_buffer_6_out = not_2_out ? adder_1_out : 12'bz;  // Controlled_Buffer controlled_buffer_6
  Controlled_Buffer #(.width(12)) controlled_buffer_7 (.out(controlled_buffer_6_out), .en(LOAD));  // open: in
endmodule
