// Logisim project 4BitDTLComputer.circ as structural Verilog: 1 circuit, main circuit main
module main (
  input  [3:0] in_1,
  input  [3:0] in_2,
  input  in_3,
  input  [3:0] in_4,
  input  [3:0] in_5,
  input  in_6,
  input  in_7
);

  wire and_1_out, CLK, decoder_1_out0, decoder_1_out1, decoder_1_out2, decoder_1_out3, decoder_1_out4,
       decoder_1_out5, decoder_1_out6, decoder_1_out7, NAND_CTRL, shift_register_1_p2, shift_register_1_p11,
       shift_register_1_p12, shift_register_1_p13;
  wire [2:0] CycleLUT_data;
  wire [3:0] A_q, B_q, controlled_buffer_1_out, controlled_buffer_2_out, INST_q, nand_1_out, or_1_out;

  Clock u_CLK (.out(CLK));
  Register #(.width(4)) INST (
    .D(in_1), .en(shift_register_1_p11), .clk(shift_register_1_p11), .Q(INST_q));  // open: clr
  Counter #(.max('hf), .width(4)) PCL ();  // open: clr, load, up, count, clk, D, carry, Q
  Counter #(.max('hf), .width(4)) PCM ();  // open: clr, load, up, count, clk, D, carry, Q
  Counter #(.max('hf), .width(4)) PCH ();  // open: clr, load, up, count, clk, D, carry, Q
  ROM #(.addrWidth(4), .dataWidth(3)) CycleLUT (.addr(in_2), .data(CycleLUT_data));
  ROM #(.addrWidth(12), .dataWidth(4)) rom_1 ();  // open: addr, data
  assign controlled_buffer_1_out = in_3 ? in_4 : 4'bz;  // Controlled_Buffer controlled_buffer_1
  assign controlled_buffer_2_out = NAND_CTRL ? nand_1_out : 4'bz;  // Controlled_Buffer controlled_buffer_2
  Decoder #(.enable("false"), .select(3)) decoder_1 (
    .out0(decoder_1_out0), .out1(decoder_1_out1), .out2(decoder_1_out2), .out3(decoder_1_out3),
    .out4(decoder_1_out4), .out5(decoder_1_out5), .out6(decoder_1_out6), .out7(decoder_1_out7),
    .sel(CycleLUT_data));
  Pull_Resistor pull_resistor_1 (.node(controlled_buffer_1_out));
  assign or_1_out = controlled_buffer_1_out | controlled_buffer_2_out;  // OR_Gate or_1, 4 bits wide
  Pull_Resistor pull_resistor_2 (.node(controlled_buffer_2_out));
  // Shift_Register #(.trigger("falling")) shift_register_1: pin names not known; wires that end beside it: CLK, shift_register_1_p2, decoder_1_out0, decoder_1_out1, decoder_1_out2, decoder_1_out3, decoder_1_out4, decoder_1_out5, decoder_1_out6, decoder_1_out7, shift_register_1_p11, shift_register_1_p12, shift_register_1_p13, shift_register_1_p2
  Register #(.width(4)) A (.D(or_1_out), .en(and_1_out), .clk(and_1_out), .Q(A_q));  // open: clr
  Register #(.width(4)) B (.D(in_5), .en(in_6), .clk(in_7), .Q(B_q));  // open: clr
  and and_1 (and_1_out, shift_register_1_p13, NAND_CTRL);
  // Probe on A_q
  Demultiplexer #(.enable("false"), .select(4)) demultiplexer_1 (
    .out0(NAND_CTRL), .in(shift_register_1_p12), .sel(INST_q));  // open: out1, out2, out3, out4, out5, out6, out7, out8, out9, out10, out11, out12, out13, out14, out15
  assign nand_1_out = ~(A_q & B_q);  // NAND_Gate nand_1, 4 bits wide
  Register #(.width(4)) SPL ();  // open: D, en, clk, Q, clr
  Register #(.width(4)) SPM ();  // open: D, en, clk, Q, clr
  Register #(.width(4)) SPH ();  // open: D, en, clk, Q, clr

  // Other names for the same wires on the sheet: DATA[3:0] = in_1
endmodule
