// Logisim project Decoding.circ as structural Verilog: 1 circuit, main circuit main
module main (
  input  RegAffected,
  input  [2:0] in_2,
  input  [3:0] in_3,
  input  Update,
  input  LoadIn,
  output A,
  output B,
  output PC01,
  output PC02,
  output PC03
);

  wire demultiplexer_1_out5, demultiplexer_1_out6, demultiplexer_1_out7;
  wire [3:0] SP01_q, SP02_q, SP03_q;

  Register #(.width(4)) SP01 (.D(in_3), .en(demultiplexer_1_out5), .clk(Update), .Q(SP01_q));  // open: clr
  Demultiplexer #(.select(3)) demultiplexer_1 (
    .out0(A), .out1(B), .out2(PC01), .out3(PC02), .out4(PC03), .out5(demultiplexer_1_out5),
    .out6(demultiplexer_1_out6), .out7(demultiplexer_1_out7), .in(RegAffected), .sel(in_2));
  Register #(.width(4)) SP02 (.D(in_3), .en(demultiplexer_1_out6), .clk(Update), .Q(SP02_q));  // open: clr
  Register #(.width(4)) SP03 (.D(in_3), .en(demultiplexer_1_out7), .clk(Update), .Q(SP03_q));  // open: clr
  Counter #(.max('hfff), .width(12)) counter_1 (
    .load(LoadIn), .clk(LoadIn), .D({SP01_q, SP02_q, SP03_q}));  // open: clr, up, count, carry, Q
endmodule
