// Logisim project PB1204.circ as structural Verilog: 1 circuit, main circuit main
module main (
  input  in_1,
  input  [3:0] RegisterBits,
  input  [3:0] FunctionBits,
  input  in_4,
  input  [3:0] DATAIN,
  output [3:0] DATAOUT,
  output [11:0] ADDRESS
);

  wire adder_1_cout, AddressRegisterHigh, AddressRegisterLow, AddressRegisterMiddle, ALUADD, ALUenable,
       ALUNAND, ALUNOR, ALUNOT, ALUShiftLeft, ALUShiftRight, ALUSwap, and_1_out, and_2_out, and_3_out,
       and_4_out, and_5_out, and_6_out, and_7_out, and_8_out, and_9_out, and_10_out, and_11_out, and_12_out,
       and_13_out, and_14_out, and_15_out, and_16_out, and_17_out, and_18_out, and_19_out, and_20_out,
       and_21_out, and_22_out, and_23_out, and_24_out, and_25_out, and_26_out, and_27_out, and_28_out,
       ARegister, BitmaskRegister, BRegister, clock_1_out, ConnectToAddressBus, DecrementRegister,
       demultiplexer_2_out8, demultiplexer_3_out1, demultiplexer_3_out2, demultiplexer_3_out3,
       demultiplexer_3_out4, IncrementRegister, InstructionRegister, InterruptModeRegister, not_1_out,
       not_2_out, or_1_out, or_2_out, or_3_out, or_4_out, ProgramCounter, ProgramCounterHigh,
       ProgramCounterLow, ProgramCounterMiddle, pull_resistor_2_node, pull_resistor_3_node,
       pull_resistor_4_node, ReadFromALUOut, ReadFromDatabus, register_5_q, ResetRegister, StackPointer,
       StackPointerRegisterHigh, StackPointerRegisterLow, StackPointerRegisterMiddle, TriggerUpdate,
       WriteToDatabus;
  wire [2:0] register_4_q;
  wire [3:0] ABuffer_q, adder_1_out, ALUOut, AOut, BBuffer_q, BOut, controlled_buffer_3_out,
       controlled_buffer_7_out, DATABUS, InstructionCounter_q, InstructionRegister_q, nand_1_out, nor_1_out,
       not_3_out, ProgramCounterHigh_q, ProgramCounterLow_q, ProgramCounterMiddle_q, register_1_q,
       register_2_q, register_3_q;
  wire [7:4] BitmaskRegister_q;
  wire [11:0] controlled_buffer_10_out, ProgramCounterRegister_q, StackPointerRegister_q;

  Controlled_Buffer #(.width(4)) controlled_buffer_1 (.in(DATAIN), .en(ReadFromDatabus));  // open: out
  and and_1 (and_1_out, ARegister, ReadFromDatabus);
  and and_2 (and_2_out, ARegister, TriggerUpdate);
  and and_3 (and_3_out, ARegister, WriteToDatabus);
  and and_4 (and_4_out, ARegister, ResetRegister);
  and and_5 (and_5_out, ARegister, ReadFromALUOut);
  and and_6 (and_6_out, BRegister, ReadFromDatabus);
  and and_7 (and_7_out, BRegister, TriggerUpdate);
  and and_8 (and_8_out, BRegister, WriteToDatabus);
  and and_9 (and_9_out, BRegister, ResetRegister);
  and and_10 (and_10_out, ResetRegister, InstructionRegister);
  Clock clock_1 (.out(clock_1_out));
  Pull_Resistor pull_resistor_1 (.node(DATABUS));
  assign DATAOUT = WriteToDatabus ? DATABUS : 4'bz;  // Controlled_Buffer controlled_buffer_2
  assign controlled_buffer_3_out = and_5_out ? ALUOut : 4'bz;  // Controlled_Buffer controlled_buffer_3
  Register #(.trigger("high"), .width(4)) ABuffer (
    .D(controlled_buffer_3_out), .en(or_1_out), .clk(or_1_out), .Q(ABuffer_q), .clr(and_4_out));
  assign controlled_buffer_3_out = and_1_out ? DATABUS : 4'bz;  // Controlled_Buffer controlled_buffer_4
  or or_1 (or_1_out, and_1_out, and_5_out);
  Counter #(.max('hf), .width(4)) InstructionCounter (
    .clr(and_10_out), .load(pull_resistor_2_node), .up(pull_resistor_3_node), .count(pull_resistor_4_node),
    .clk(clock_1_out), .Q(InstructionCounter_q));  // open: D, carry
  Pull_Resistor pull_resistor_2 (.node(pull_resistor_2_node));
  Pull_Resistor #(.pull(1)) pull_resistor_3 (.node(pull_resistor_3_node));
  Pull_Resistor #(.pull(1)) pull_resistor_4 (.node(pull_resistor_4_node));
  and and_11 (and_11_out, BitmaskRegister, ReadFromDatabus);
  and and_12 (and_12_out, InstructionRegister, ReadFromDatabus);
  and and_13 (and_13_out, InstructionRegister, ResetRegister);
  RAM #(.addrWidth(12), .dataWidth(4), .databus("bidir"), .trigger("high")) ram_1 (
    .addr(ADDRESS), .we(WriteToDatabus), .oe(ReadFromDatabus), .data(DATABUS));
  Register #(.width(4)) BBuffer (.D(DATABUS), .en(and_6_out), .clk(and_6_out), .Q(BBuffer_q), .clr(and_9_out));
  Register #(.trigger("high"), .width(4)) u_BitmaskRegister (
    .D(DATABUS), .en(and_11_out), .clk(and_11_out), .Q(BitmaskRegister_q), .clr(and_13_out));
  Register #(.trigger("high"), .width(4)) u_InstructionRegister (
    .D(DATABUS), .en(and_12_out), .clk(and_12_out), .Q(InstructionRegister_q), .clr(and_13_out));
  Register #(.width(4)) u_ARegister (.D(ABuffer_q), .en(and_2_out), .clk(and_2_out), .Q(AOut), .clr(and_4_out));
  Register #(.width(4)) u_BRegister (.D(BBuffer_q), .en(and_7_out), .clk(and_7_out), .Q(BOut), .clr(and_9_out));
  assign DATABUS = and_3_out ? AOut : 4'bz;  // Controlled_Buffer controlled_buffer_5
  assign DATABUS = and_8_out ? BOut : 4'bz;  // Controlled_Buffer controlled_buffer_6
  ROM #(.addrWidth(12), .dataWidth(9)) rom_1 (.addr({InstructionRegister_q, BitmaskRegister_q, InstructionCounter_q}));  // open: data
  assign controlled_buffer_7_out = in_4 ? RegisterBits : 4'bz;  // Controlled_Buffer controlled_buffer_7
  assign controlled_buffer_7_out = not_1_out ? BitmaskRegister_q : 4'bz;  // Controlled_Buffer controlled_buffer_8
  not not_1 (not_1_out, in_4);
  Register #(.width(4)) u_ProgramCounterLow (
    .D(DATABUS), .en(and_14_out), .clk(and_14_out), .Q(ProgramCounterLow_q));  // open: clr
  and and_14 (and_14_out, ProgramCounterLow, ReadFromDatabus);
  Register #(.width(4)) u_ProgramCounterMiddle (
    .D(DATABUS), .en(and_15_out), .clk(and_15_out), .Q(ProgramCounterMiddle_q));  // open: clr
  and and_15 (and_15_out, ProgramCounterMiddle, ReadFromDatabus);
  Register #(.width(4)) u_ProgramCounterHigh (
    .D(DATABUS), .en(and_16_out), .clk(and_16_out), .Q(ProgramCounterHigh_q));  // open: clr
  and and_16 (and_16_out, ProgramCounterHigh, ReadFromDatabus);
  and and_17 (and_17_out, ProgramCounter, TriggerUpdate);
  and and_18 (and_18_out, ProgramCounter, IncrementRegister);
  and and_19 (and_19_out, ProgramCounter, ResetRegister);
  Pull_Resistor pull_resistor_5 (.node(ALUenable));
  assign ALUenable = in_1 ? FunctionBits[3] : 1'bz;  // Controlled_Buffer controlled_buffer_9
  Demultiplexer #(.select(4)) demultiplexer_1 (
    .out0(InstructionRegister), .out1(InterruptModeRegister), .out2(AddressRegisterLow),
    .out3(AddressRegisterMiddle), .out4(AddressRegisterHigh), .out5(ProgramCounter), .out6(StackPointer),
    .out7(BitmaskRegister), .out8(ARegister), .out9(BRegister), .out10(ProgramCounterLow),
    .out11(ProgramCounterMiddle), .out12(ProgramCounterHigh), .out13(StackPointerRegisterLow),
    .out14(StackPointerRegisterMiddle), .out15(StackPointerRegisterHigh), .in(in_1),
    .sel(controlled_buffer_7_out));
  Demultiplexer #(.select(4)) demultiplexer_2 (
    .out0(ConnectToAddressBus), .out1(ReadFromDatabus), .out2(WriteToDatabus), .out3(TriggerUpdate),
    .out4(IncrementRegister), .out5(DecrementRegister), .out6(ResetRegister), .out7(ReadFromALUOut),
    .out8(demultiplexer_2_out8), .out9(ALUNAND), .out10(ALUNOR), .out11(ALUNOT), .out12(ALUADD),
    .out13(ALUShiftLeft), .out14(ALUShiftRight), .out15(ALUSwap), .in(in_1), .sel(FunctionBits));
  or or_2 (or_2_out, and_17_out, and_18_out);
  Counter #(.max('hfff), .width(12)) ProgramCounterRegister (
    .clr(and_19_out), .load(and_17_out), .up(and_18_out), .clk(or_2_out),
    .D({ProgramCounterHigh_q, ProgramCounterMiddle_q, ProgramCounterLow_q}), .Q(ProgramCounterRegister_q));  // open: count, carry
  and and_20 (and_20_out, ConnectToAddressBus, ProgramCounter);
  or or_3 (or_3_out, and_20_out, and_28_out);
  assign controlled_buffer_10_out = and_20_out ? ProgramCounterRegister_q : 12'bz;  // Controlled_Buffer controlled_buffer_10
  Register #(.width(4)) register_1 (.D(DATABUS), .en(and_21_out), .clk(and_21_out), .Q(register_1_q));  // open: clr
  and and_21 (and_21_out, StackPointerRegisterLow, ReadFromDatabus);
  Register #(.width(4)) register_2 (.D(DATABUS), .en(and_22_out), .clk(and_22_out), .Q(register_2_q));  // open: clr
  and and_22 (and_22_out, StackPointerRegisterMiddle, ReadFromDatabus);
  Register #(.width(4)) register_3 (.D(DATABUS), .en(and_23_out), .clk(and_23_out), .Q(register_3_q));  // open: clr
  and and_23 (and_23_out, StackPointerRegisterHigh, ReadFromDatabus);
  and and_24 (and_24_out, StackPointer, TriggerUpdate);
  and and_25 (and_25_out, StackPointer, ResetRegister);
  and and_26 (and_26_out, StackPointer, IncrementRegister);
  and and_27 (and_27_out, StackPointer, DecrementRegister);
  Register #(.width(3)) register_4 (
    .D(FunctionBits[2:0]), .en(ALUenable), .clk(ALUenable), .Q(register_4_q));  // open: clr
  Demultiplexer #(.select(3)) demultiplexer_3 (
    .out1(demultiplexer_3_out1), .out2(demultiplexer_3_out2), .out3(demultiplexer_3_out3),
    .out4(demultiplexer_3_out4), .in(ReadFromALUOut), .sel(register_4_q));  // open: out0, out5, out6, out7
  Register #(.trigger("falling"), .width(1)) register_5 (
    .D(adder_1_cout), .en(not_2_out), .clk(not_2_out), .Q(register_5_q));  // open: clr
  not not_2 (not_2_out, ALUADD);
  assign nand_1_out = ~(AOut & BOut);  // NAND_Gate nand_1, 4 bits wide
  assign ALUOut = demultiplexer_3_out1 ? nand_1_out : 4'bz;  // Controlled_Buffer controlled_buffer_11
  assign nor_1_out = ~(AOut | BOut);  // NOR_Gate nor_1, 4 bits wide
  assign ALUOut = demultiplexer_3_out2 ? nor_1_out : 4'bz;  // Controlled_Buffer controlled_buffer_12
  assign not_3_out = ~AOut;  // NOT_Gate not_3, 4 bits wide
  Adder #(.width(4)) adder_1 (.a(AOut), .b(BOut), .out(adder_1_out), .cin(register_5_q), .cout(adder_1_cout));
  Counter #(.max('hfff), .width(12)) StackPointerRegister (
    .clr(and_25_out), .load(and_24_out), .up(and_26_out), .count(1'b1), .clk(or_4_out),
    .D({register_3_q, register_2_q, register_1_q}), .Q(StackPointerRegister_q));  // open: carry
  or or_4 (or_4_out, and_24_out, and_26_out, and_27_out);
  assign ALUOut = demultiplexer_3_out3 ? not_3_out : 4'bz;  // Controlled_Buffer controlled_buffer_13
  assign ALUOut = demultiplexer_3_out4 ? adder_1_out : 4'bz;  // Controlled_Buffer controlled_buffer_14
  assign controlled_buffer_10_out = and_28_out ? StackPointerRegister_q : 12'bz;  // Controlled_Buffer controlled_buffer_15
  Pull_Resistor pull_resistor_6 (.node(ALUOut));
  and and_28 (and_28_out, ConnectToAddressBus, StackPointer);
  Counter #(.max('hfff), .width(12)) AddressRegister (
    .load(or_3_out), .clk(or_3_out), .D(controlled_buffer_10_out), .Q(ADDRESS));  // open: clr, up, count, carry

  // Other names for the same wires on the sheet: ADDRESSBUS[11:0] = ADDRESS; ALUmode[2:0] = FunctionBits[2:0]

  // Notes on the sheet:
  //   Nothing
endmodule
